# Fritzing sketch MiniCar_ESP32-C3 (saved by Fritzing 0.9.5d)
stripboards: 1

parts:
  J4 = female pin header, 16 pins [form="♀ (female)"]
  J8 = female pin header, 2 pins [form="♀ (female)"]
  J9 = female pin header, 2 pins [form="♀ (female)"]
  J10 = female pin header, 16 pins [form="♀ (female)"]
  J13 = Screw terminal - 2 pins [package=THT]
  S1 = Toggle Switch [package=THT]
  J15 = male pin header, 16 pins [form="♂ (male)"]
  J16 = male pin header, 16 pins [form="♂ (male)"]
  J1 = female pin header, 4 pins [form="♀ (female)"]
  J17 = female pin header, 4 pins [form="♀ (female)"]
  Adafruit_Atmega32u1 = Adafruit Atmega32u4 Breakout Board [part_number="Atmega 32u4"]
  VCC1 = Battery
  U1 = SPI_FLASH-X25XX [package=so08]
  R1 = Resistor [tolerance=±5% resistance=220 package=THT]
  LED1 = LED - 5mm [color="Red (633nm)" package="5 mm [THT]"]

nets:
  N1: J4.pin1, J10.pin1, J15.pin1, J16.pin1
  N2: J4.pin2, J10.pin2, J15.pin2, J16.pin2, Adafruit_Atmega32u1.5V, Adafruit_Atmega32u1.3V
  N3: J4.pin3, J10.pin3, J15.pin3, J16.pin3, Adafruit_Atmega32u1.A, Adafruit_Atmega32u1.E6
  N4: J4.pin4, J10.pin4, J15.pin4, J16.pin4, Adafruit_Atmega32u1.F0, Adafruit_Atmega32u1.B0
  N5: J4.pin5, J10.pin5, J15.pin5, J16.pin5, Adafruit_Atmega32u1.F1, Adafruit_Atmega32u1.B1
  N6: J4.pin6, J10.pin6, J15.pin6, J16.pin6, Adafruit_Atmega32u1.F4, Adafruit_Atmega32u1.B2
  N7: J4.pin7, J10.pin7, J15.pin7, J16.pin7, Adafruit_Atmega32u1.F5, Adafruit_Atmega32u1.B3
  N8: J4.pin8, J10.pin8, J15.pin8, J16.pin8, Adafruit_Atmega32u1.F6, Adafruit_Atmega32u1.D0
  N9: J4.pin9, J10.pin9, J15.pin9, J16.pin9, Adafruit_Atmega32u1.F7, Adafruit_Atmega32u1.D1
  N10: J4.pin10, J10.pin10, J15.pin10, J16.pin10, Adafruit_Atmega32u1.C7, Adafruit_Atmega32u1.D2
  N11: J4.pin11, J10.pin11, J15.pin11, J16.pin11, Adafruit_Atmega32u1.C6, Adafruit_Atmega32u1.D3
  N12: J4.pin12, J10.pin12, J15.pin12, J16.pin12, Adafruit_Atmega32u1.B7, Adafruit_Atmega32u1.D4
  N13: J4.pin13, J10.pin13, J15.pin13, J16.pin13, Adafruit_Atmega32u1.B6, Adafruit_Atmega32u1.D5
  N14: J4.pin14, J9.pin1, J9.pin2, J10.pin14, J13.pin2, S1.L1, S1.COM, S1.L2, J15.pin14, J16.pin14, J1.pin4, J17.pin4, Adafruit_Atmega32u1.B5, Adafruit_Atmega32u1.D6, VCC1.+, U1.GND, U1.MOSI, R1.Pin_0
  N15: J4.pin15, J10.pin15, J15.pin15, J16.pin15, Adafruit_Atmega32u1.B4, Adafruit_Atmega32u1.D7
  N16: J4.pin16, J10.pin16, J15.pin16, J16.pin16, Adafruit_Atmega32u1.GND
  N17: J8.pin1, J8.pin2, J13.pin1, J1.pin1, J1.pin3, J17.pin1, J17.pin3, VCC1.-, U1.CS, U1.WP, U1.SCK, U1.VCC, LED1.cathode
  N18: J1.pin2, J17.pin2, U1.MISO, U1.HOLD
  N19: Adafruit_Atmega32u1.VCC, Adafruit_Atmega32u1.RST
  N20: R1.Pin_1, LED1.anode
