# Fritzing sketch MiniCar_comopenent (saved by Fritzing 0.9.5d)
circuit board: 8.46667cm x 5.64444cm
stripboards: 1

parts:
  J3 = female pin header, 6 pins [form="♀ (female)"]
  J6 = female pin header, 2 pins [form="♀ (female)"]
  J11 = Screw terminal - 2 pins [package=THT]
  J12 = Screw terminal - 2 pins [package=THT]
  HC-SR04_Sensor_1 = HC-SR04 Ultrasonic Distance Sensor
  元件1 = Motor Driver 1A Dual TB6612FNG
  J14 = female pin header, 4 pins [form="♀ (female)"]
  M1 = DC Motor
  M2 = DC Motor
  J19 = female pin header, 3 pins [form="♀ (female)"]
  Grove1 = Grove 4 Digit Display
  IR1 = TSOP312.., 314.. [package=THT]
  J20 = female pin header, 2 pins [form="♀ (female)"]
  J7-5v_power_input = female pin header, 2 pins [form="♀ (female)"]
  J18 = female pin header, 4 pins [form="♀ (female)"]
  J2 = female pin header, 2 pins [form="♀ (female)"]

nets (from the breadboard view):
  VCC: J3.pin1, J3.pin2, HC-SR04_Sensor_1.VCC, HC-SR04_Sensor_1.TRIG, 元件1.A02, 元件1.A01, 元件1.VM, 元件1.BIN1, 元件1.BIN2, J14.pin3, J14.pin4, Grove1.VCC, Grove1.DIO, J20.pin1, J7-5v_power_input.pin2, J18.pin2, J18.pin3, J2.pin1
  N1: J3.pin3, 元件1.STBY, J18.pin4
  N2: J3.pin4, 元件1.AIN1
  N3: J3.pin5, 元件1.AIN2
  N4: J6.pin1, J19.pin2, IR1.Vs
  N5: J6.pin2, J19.pin3, IR1.Data
  N6: J11.pin1, 元件1.B01, M1.pin_2
  N7: J11.pin2, 元件1.B02, M1.pin_1
  N8: J12.pin1, M2.pin_2
  N9: J12.pin2, M2.pin_1
  GND: HC-SR04_Sensor_1.ECHO, HC-SR04_Sensor_1.GND, 元件1.GND, J14.pin1, J14.pin2, Grove1.GND, Grove1.CLK, J7-5v_power_input.pin1, J18.pin1, J2.pin2
  N10: J19.pin1, IR1.GND
