# Fritzing sketch MiniCar_llinked_lines (saved by Fritzing 0.9.5d)
stripboards: 2

parts:
  J2 = female pin header, 2 pins [form="♀ (female)"]
  J3 = female pin header, 6 pins [form="♀ (female)"]
  J6 = female pin header, 2 pins [form="♀ (female)"]
  J7 = female pin header, 2 pins [form="♀ (female)"]
  J11 = Screw terminal - 2 pins [package=THT]
  J12 = Screw terminal - 2 pins [package=THT]
  HC-SR04_Sensor_1 = HC-SR04 Ultrasonic Distance Sensor
  元件1 = Motor Driver 1A Dual TB6612FNG  # not connected
  J14 = female pin header, 4 pins [form="♀ (female)"]  # not connected
  M1 = DC Motor
  M2 = DC Motor
  J18 = female pin header, 4 pins [form="♀ (female)"]
  J19 = female pin header, 3 pins [form="♀ (female)"]
  Grove1 = Grove 4 Digit Display
  IR1 = TSOP312.., 314.. [package=THT]
  J20 = female pin header, 2 pins [form="♀ (female)"]
  R2 = Resistor [tolerance=±5% resistance=220 package=THT]
  LED2 = LED - 5mm [color="Red (633nm)" package="5 mm [THT]"]
  J21 = female pin header, 4 pins [form="♀ (female)"]
  J22 = female pin header, 4 pins [form="♀ (female)"]
  J23 = female pin header, 2 pins [form="♀ (female)"]
  J24 = female pin header, 2 pins [form="♀ (female)"]
  J25 = male pin header, 16 pins [form="♂ (male)"]
  J26 = male pin header, 16 pins [form="♂ (male)"]
  J27 = female pin header, 16 pins [form="♀ (female)"]
  J28 = female pin header, 16 pins [form="♀ (female)"]
  J29 = Screw terminal - 2 pins [package=THT]
  S2 = Toggle Switch [package=THT]
  Adafruit_Atmega32u2 = Adafruit Atmega32u4 Breakout Board [part_number="Atmega 32u4"]
  VCC2 = Battery
  U2 = SPI_FLASH-X25XX [package=so08]

nets:
  N1: J2.pin1, J25.pin10, J26.pin10, J27.pin10, J28.pin10, Adafruit_Atmega32u2.C6, Adafruit_Atmega32u2.D3
  N2: J2.pin2, J3.pin4, R2.Pin_0, J25.pin14, J26.pin14, J27.pin14, J28.pin14, Adafruit_Atmega32u2.B4, Adafruit_Atmega32u2.D7
  N3: J3.pin1, HC-SR04_Sensor_1.ECHO, J18.pin2, Grove1.VCC, J25.pin12, J26.pin12, J27.pin12, J28.pin12, Adafruit_Atmega32u2.B6, Adafruit_Atmega32u2.D5
  N4: J3.pin2, HC-SR04_Sensor_1.TRIG, J18.pin3, Grove1.DIO, J25.pin13, J26.pin13, J27.pin13, J28.pin13, Adafruit_Atmega32u2.B5, Adafruit_Atmega32u2.D6
  N5: J3.pin3, J3.pin5, J25.pin15, J26.pin15, J27.pin15, J28.pin15, Adafruit_Atmega32u2.GND
  N6: J6.pin1, J19.pin3, IR1.Data
  N7: J6.pin2, J25.pin7, J26.pin7, J27.pin7, J28.pin7, Adafruit_Atmega32u2.F6, Adafruit_Atmega32u2.D0
  N8: J7.pin1, J21.pin1, J22.pin1, J24.pin1, J24.pin2, U2.CS, U2.VCC
  N9: J7.pin2, J21.pin3, J21.pin4, J22.pin3, J22.pin4, J23.pin1, J23.pin2, J29.pin1, J29.pin2, VCC2.-, VCC2.+, U2.WP, U2.GND, U2.MOSI, U2.SCK
  N10: J11.pin1, M1.pin_2
  N11: J11.pin2, M1.pin_1
  N12: J12.pin1, M2.pin_2
  N13: J12.pin2, M2.pin_1
  N14: HC-SR04_Sensor_1.VCC, J18.pin4, Grove1.CLK
  GND: HC-SR04_Sensor_1.GND, J18.pin1, Grove1.GND
  N15: J19.pin1, IR1.GND
  N16: J19.pin2, IR1.Vs
  N17: J20.pin1, J25.pin5, J26.pin5, J27.pin5, J28.pin5, Adafruit_Atmega32u2.F4, Adafruit_Atmega32u2.B2
  N18: J20.pin2, J25.pin6, J26.pin6, J27.pin6, J28.pin6, Adafruit_Atmega32u2.F5, Adafruit_Atmega32u2.B3
  N19: R2.Pin_1, LED2.anode
  N20: J21.pin2, J22.pin2, U2.MISO, U2.HOLD
  N21: J25.pin1, J26.pin1, J27.pin1, J28.pin1, Adafruit_Atmega32u2.5V, Adafruit_Atmega32u2.3V
  N22: J25.pin2, J26.pin2, J27.pin2, J28.pin2, Adafruit_Atmega32u2.A, Adafruit_Atmega32u2.E6
  N23: J25.pin3, J26.pin3, J27.pin3, J28.pin3, Adafruit_Atmega32u2.F0, Adafruit_Atmega32u2.B0
  N24: J25.pin4, J26.pin4, J27.pin4, J28.pin4, Adafruit_Atmega32u2.F1, Adafruit_Atmega32u2.B1
  N25: J25.pin8, J26.pin8, J27.pin8, J28.pin8, Adafruit_Atmega32u2.F7, Adafruit_Atmega32u2.D1
  N26: J25.pin9, J26.pin9, J27.pin9, J28.pin9, Adafruit_Atmega32u2.C7, Adafruit_Atmega32u2.D2
  N27: J25.pin11, J26.pin11, J27.pin11, J28.pin11, Adafruit_Atmega32u2.B7, Adafruit_Atmega32u2.D4
  N28: J25.pin16, J26.pin16, J27.pin16, J28.pin16, Adafruit_Atmega32u2.VCC, Adafruit_Atmega32u2.RST
  N29: S2.L1, S2.COM, S2.L2
