# Fritzing sketch small_car (saved by Fritzing 0.9.5d)
breadboards: 2

parts:
  M1 = DC Motor  # not connected
  M3 = DC Motor  # not connected
  R1 = Resistor [tolerance=±5% resistance=220 package=THT]
  R2 = Resistor [tolerance=±5% resistance=220 package=THT]
  C1 = Ceramic Capacitor [capacitance=100nF package="100 mil [THT, multilayer]"]
  C2 = Electrolytic Capacitor [capacitance=1µF package="100 mil [THT, electrolytic]"]
  元件1 = Arduino Pro Mini v13
  LED1 = LED - 5mm [color="Red (633nm)" package="5 mm [THT]"]
  J1 = Piezo Speaker
  U1 = 74HC04_HEX_INVERTER [package=dil14]
  HC-SR04_Sensor_1 = HC-SR04 Ultrasonic Distance Sensor
  IR1 = TSOP312.., 314.. [package=THT]
  LED2 = LED - 5mm [color="Red (633nm)" package="5 mm [THT]"]
  R3 = Resistor [tolerance=±5% resistance=220 package=THT]

nets:
  N1: R1.Pin_0, LED2.cathode
  N2: R2.Pin_0, LED1.anode
  N3: C1.0, U1.GND
  N4: C2.-, U1.2Y, R3.Pin_1
  N5: 元件1.D9_PWM, HC-SR04_Sensor_1.ECHO
  N6: 元件1.D7, IR1.GND
  N7: LED1.cathode, J1.pin1, HC-SR04_Sensor_1.GND, IR1.Vs, LED2.anode, R3.Pin_0
  N8: J1.pin2, U1.3Y
  N9: HC-SR04_Sensor_1.VCC, IR1.Data
