# Fritzing sketch PowerBox2024-new-1 (saved by Fritzing 0.9.5d)
circuit board: 8.46667cm x 5.64444cm
breadboards: 1

parts:
  Arduino_Uno = Arduino Uno (Rev3)
  J4-power_low_side = Screw terminal - 2 pins [package=THT]
  J6-power-high_side = Screw terminal - 2 pins [package=THT]
  IC1 = 11LC160 [package=THT]
  IC2 = 11LC160 [package=THT]
  LCD1-1602A = LCD screen
  potentiometer = POT [package=pot_mammoth]
  relay = RELAY-SOLIDSTATE [package=relay-s108t02]
  R11 = Resistor [tolerance=±5% resistance=1000000 package=THT]
  R12 = Resistor [tolerance=±5% resistance=1000000 package=THT]  # not connected
  R13 = Resistor [tolerance=±5% resistance=1000 package=THT]  # not connected
  R14 = Resistor [tolerance=±5% resistance=1000 package=THT]
  R5-sampling = Resistor [tolerance=±5% resistance=0.2 package=THT]
  R-220 = Resistor [tolerance=±5% resistance=220 package=THT]
  J1-fire = screw terminal, 3 pins
  J2-middle = screw terminal, 3 pins
  J5-sigal = screw terminal, 3 pins

nets (from the breadboard view):
  N1: Arduino_Uno.A0, IC1.N/C#2, J5-sigal.pin2
  N2: Arduino_Uno.A1, IC2.N/C#2, J5-sigal.pin3
  N3: Arduino_Uno.D8, R-220.Pin_0, J5-sigal.pin1
  N4: Arduino_Uno.D11_PWM/MOSI, LCD1-1602A.E
  N5: Arduino_Uno.D12/MISO, LCD1-1602A.RS
  N6: Arduino_Uno.D2, LCD1-1602A.DB7
  N7: Arduino_Uno.D3_PWM, LCD1-1602A.DB6
  N8: Arduino_Uno.D4, LCD1-1602A.DB5
  N9: Arduino_Uno.D5_PWM, LCD1-1602A.DB4
  5V: Arduino_Uno.5V, J4-power_low_side.pin2, J6-power-high_side.pin2, IC1.N/C#1, IC1.0V, IC1.SCIO_-_Data_I/O, IC2.N/C#1, IC2.0V, IC2.SCIO_-_Data_I/O, LCD1-1602A.VDD, LCD1-1602A.LED+, potentiometer.S
  GND: Arduino_Uno.GND, J4-power_low_side.pin1, J6-power-high_side.pin1, IC1.N/C#0, IC1.+V, IC2.N/C#0, IC2.+V, LCD1-1602A.VSS, LCD1-1602A.R/W, LCD1-1602A.LED-, potentiometer.E, relay.-
  N10: IC1.N/C#5, IC2.N/C#5, R14.Pin_1, R5-sampling.Pin_1, J2-middle.pin3
  N11: IC1.N/C#6, R5-sampling.Pin_0, J1-fire.pin3
  N12: IC2.N/C#6, R14.Pin_0
  N13: LCD1-1602A.V0, potentiometer.A
  N14: relay.T1, J1-fire.pin2
  N15: relay.T2, R11.Pin_0, J2-middle.pin2
  N16: relay.+, R-220.Pin_1

notes:
  电源插头
  接线板
  继电器，光偶低压侧供电
  光偶高压侧供电
  电压
  电流
  火线
  中线
  地线
  3接线柱版本
