# Fritzing sketch PowerBox2024-new (saved by Fritzing 0.9.5d)
circuit board: 8.46667cm x 5.64444cm
breadboards: 1
perfboards: 1

parts:
  Arduino_Uno = Arduino Uno (Rev3)
  J4-power_low_side = Screw terminal - 2 pins [package=THT]
  J5-sigal = Screw terminal - 2 pins [package=THT]
  J6-power-high_side = Screw terminal - 2 pins [package=THT]
  J2-middle = Screw terminal - 2 pins [package=THT]
  IC1 = 11LC160 [package=THT]
  IC2 = 11LC160 [package=THT]
  J3-继电器P3 = Screw terminal - 2 pins [package=THT]
  LCD1-1602A = LCD screen
  potentiometer = POT [package=pot_mammoth]
  relay = RELAY-SOLIDSTATE [package=relay-s108t02]
  R11 = Resistor [tolerance=±5% resistance=1000000 package=THT]
  R12 = Resistor [tolerance=±5% resistance=1000000 package=THT]
  R13 = Resistor [tolerance=±5% resistance=1000 package=THT]
  R14 = Resistor [tolerance=±5% resistance=1000 package=THT]
  R5-sampling = Resistor [tolerance=±5% resistance=0.2 package=THT]
  J1-fire = Screw terminal - 2 pins [package=THT]
  R-220 = Resistor [tolerance=±5% resistance=220 package=THT]

nets (from the schematic view):
  N1: Arduino_Uno.A0, J5-sigal.pin1, IC1.N/C#2
  N2: Arduino_Uno.A1, J5-sigal.pin2, IC2.N/C#2
  N3: Arduino_Uno.D8, J3-继电器P3.pin1, R-220.Pin_0
  N4: Arduino_Uno.D5_PWM, LCD1-1602A.DB4
  5V: Arduino_Uno.5V, J4-power_low_side.pin1, J4-power_low_side.pin2, J6-power-high_side.pin2, IC2.N/C#0, IC2.N/C#1, IC2.0V, IC2.SCIO_-_Data_I/O, IC2.+V, LCD1-1602A.VSS, LCD1-1602A.VDD, potentiometer.S, potentiometer.E
  N5: Arduino_Uno.GND, LCD1-1602A.LED+, LCD1-1602A.LED-
  N6: J6-power-high_side.pin1, IC1.N/C#0, IC1.N/C#1, IC1.0V, IC1.SCIO_-_Data_I/O
  N7: J2-middle.pin1, relay.T2, R11.Pin_0
  N8: J2-middle.pin2, IC1.N/C#5, IC2.N/C#5, R14.Pin_1, R5-sampling.Pin_1
  N9: IC1.N/C#6, R5-sampling.Pin_0, J1-fire.pin2
  N10: IC2.N/C#6, R13.Pin_1, R14.Pin_0
  N11: LCD1-1602A.V0, potentiometer.A
  N12: relay.T1, J1-fire.pin1
  N13: relay.+, R-220.Pin_1
  N14: R11.Pin_1, R12.Pin_0
  N15: R12.Pin_1, R13.Pin_0

notes:
  电源插头
  接线板
  光偶低压侧继电器供电
  继电器P3到单片机P8
  光偶高压侧供电
  信号到单片机
  电压
  电流
  火线
  中线
  插头地线直接接线板地线
  地线
