# Fritzing sketch small_car (saved by Fritzing 0.9.3b)
breadboards: 2

parts:
  M1 = DC Motor  # not connected
  M3 = DC Motor  # not connected
  R1 = Resistor [tolerance=±5% resistance=220 package=THT]  # not connected
  R2 = Resistor [tolerance=±5% resistance=220 package=THT]  # not connected
  C1 = Ceramic Capacitor [capacitance=100nF package="100 mil [THT, multilayer]"]  # not connected
  C2 = Electrolytic Capacitor [capacitance=1µF package="100 mil [THT, electrolytic]"]  # not connected
  元件1 = Arduino Pro Mini v13  # not connected
  LED1 = LED - 5mm [color="Red (633nm)" package="5 mm [THT]"]
  LED2 = LED - 5mm [color="Red (633nm)" package="5 mm [THT]"]
  J1 = Piezo Speaker  # not connected
  U1 = 74HC04_HEX_INVERTER [package=dil14]  # not connected

nets:
  N1: LED1.cathode, LED2.anode
